# Fritzing sketch HC-SR04 (saved by Fritzing 1.0.4)
breadboards: 1

parts:
  A1 = photon2
  LED1 = smd LED [color="Red (633nm)" package="0603 [SMD]"]
  R1 = Resistor [tolerance=±5% resistance=220 package="1206 [SMD]"]
  Part1 = SRF05 Ultrasonic Rangefinder

nets:
  N1: A1.Pin_4, A1.Pin_30, R1.Pin_1, Part1.GND
  N2: A1.Pin_12, Part1.Echo
  N3: A1.Pin_13, Part1.Trig
  N4: A1.Pin_18, LED1.cathode
  N5: A1.Pin_26, Part1.VCC
  N6: A1.Pin_28, A1.Pin_29
  N7: LED1.anode, R1.Pin_0

custom parts:
  photon2: The Photon 2 is a development module with a microcontroller and Wi-Fi networking.
