# Fritzing sketch Speed_Monitor_w8x8_NeoPixel (saved by Fritzing 1.0.4)
breadboards: 1

parts:
  A1 = photon2
  LED1 = smd LED [color="Green (570nm)" package="0603 [SMD]"]
  R1 = Resistor [tolerance=±5% resistance=220 package="1206 [SMD]"]
  Part1 = SRF05 Ultrasonic Rangefinder
  Part2 = SRF05 Ultrasonic Rangefinder
  OLED_I2C1 = OLED 128x64 I2C Monochrome Display
  U1 = WS2812 RGB LED matrix 8x8

nets:
  N1: A1.Pin_2, A1.Pin_31, OLED_I2C1.VDD
  GND: A1.Pin_4, A1.Pin_30, A1.Pin_35, R1.Pin_1, Part1.GND, Part2.GND, OLED_I2C1.GND
  N2: A1.Pin_14, Part1.Echo
  N3: A1.Pin_15, Part1.Trig
  N4: A1.Pin_17, OLED_I2C1.SDA
  N5: A1.Pin_18, OLED_I2C1.SCK
  N6: A1.Pin_19, U1.DIN
  N7: A1.Pin_21, LED1.anode
  N8: A1.Pin_23, Part2.Echo
  N9: A1.Pin_24, Part2.Trig
  VCC: A1.Pin_26, Part1.VCC, Part2.VCC, U1.VCC
  N10: A1.Pin_28, A1.Pin_29
  N11: LED1.cathode, R1.Pin_0

custom parts:
  photon2: The Photon 2 is a development module with a microcontroller and Wi-Fi networking.
  WS2812 RGB LED matrix 8x8: WS2812 matrix 8x8
